# Fritzing sketch HelloAnalogRead (saved by Fritzing 0.9.3b)
breadboards: 1

parts:
  Part1 = Arduino Nano (Rev3.0)
  Part2 = Thumb Joystick

nets:
  GND: Part1.GND, Part2.GND
  5V: Part1.5V, Part2.VCC
  N1: Part1.A0, Part2.HORZ, Part2.VERT
