# Fritzing sketch External Interrupts Test Circuit (saved by Fritzing 0.9.3b)
breadboards: 1

parts:
  Part1 = Arduino Nano (Rev3.0)
  S1 = Pushbutton [package="[THT]"]
  LED1 = LED - 5mm [color="Red (633nm)" package="5 mm [THT]"]

nets:
  N1: Part1.GND, LED1.cathode
  N2: Part1.D4, S1.Pin_1, S1.Pin_2, LED1.anode
  N3: Part1.3V3, S1.Pin_3, S1.Pin_4
