# Fritzing sketch HelloInput (saved by Fritzing 0.9.3b)
breadboards: 1

parts:
  Part1 = Arduino Nano (Rev3.0)
  S1 = Pushbutton [package="[SMD]"]

nets:
  N1: Part1.3V3, S1.Pin_1, S1.Pin_2
  N2: Part1.D13/SCK, S1.Pin_3, S1.Pin_4

notes:
  When the button closes the circuit, the pin D13 or PORTB5 is 1 (HIGH).
