# Fritzing sketch MCP3008 Circuit (saved by Fritzing 0.9.3b)
breadboards: 1

parts:
  Nano1 = Arduino Nano v2.3
  IC1 = MCP3008 8-channel 10-bit ADC [part_number=MCP3008]
  U1 = POT [package=alps_pot]
  Mod1 = KY-023 Dual Axis Joystick Module [package="Breakout board"]

nets:
  GND: Nano1.GND, IC1.no_name_yet#9, IC1.no_name_yet#14, U1.A, Mod1.GND, Mod1.VRy
  N1: Nano1.D9, IC1.no_name_yet#10
  N2: Nano1.D10, IC1.no_name_yet#11
  N3: Nano1.D11, IC1.no_name_yet#12
  N4: Nano1.D13, IC1.no_name_yet#13
  N5: Nano1.+5V, IC1.no_name_yet#15, IC1.no_name_yet#16, U1.E
  N6: IC1.no_name_yet#1, U1.S
  N7: IC1.no_name_yet#2, Mod1.+5V
  N8: IC1.no_name_yet#3, Mod1.VRx

notes:
  Not-included in code

custom parts:
  KY-023 Dual Axis Joystick Module: KY-023 Dual-Axis Joystick Module.
