# Fritzing sketch TIP122Avr (saved by Fritzing 0.9.3b)
breadboards: 1

parts:
  U1 = atmega328 [package=dip]
  VCC1 = Battery block 9V
  U2 = Voltage Regulator [package=to220-igo]  # not connected
  U2_2 = Voltage Regulator [package=to220-adj]  # not connected
  S1 = Pushbutton [package="[THT]"]
  R1 = Resistor [tolerance=±5% resistance=2 package="2010 [SMD]"]
  R1_2 = Resistor [tolerance=±5% resistance=3 package=THT]
  Q1 = npn-Powertransistor [package="TO220 [THT]"]
  LED1 = LED - 3mm [color="Red (633nm)" package="3 mm [THT]"]
  R2 = Resistor [tolerance=±5% resistance=330 package=THT]

nets:
  N1: U1.XLAT1, S1.Pin_3, S1.Pin_4
  N2: U1.XLAT2, R1.Pin_1, R1_2.Pin_1
  N3: U1.A3, Q1.base
  N4: VCC1.-, S1.Pin_2, Q1.emitter
  N5: VCC1.+, LED1.anode
  N6: R1.Pin_0, R1_2.Pin_0
  N7: Q1.collector, R2.Pin_1
  N8: LED1.cathode, R2.Pin_0

notes:
  MOSI - of the usbAsp
  MISO - of the usbAsp
  CLK - of the usbAsp
  LM7806
  300 mAmps
