# Fritzing sketch TIP122AvrCircuit (saved by Fritzing 0.9.3b)
breadboards: 1

parts:
  Q1 = npn-Powertransistor [part_number=TIP122 package="TO220 [THT]"]
  U1 = atmega328 [package=dip]
  VCC1 = Battery block 9V
  U2 = Voltage Regulator - Variable [part_number=LM7806CV package="TO220 [THT]"]
  R1 = Resistor [tolerance=±5% resistance=3 package=THT]
  R2 = Resistor [tolerance=±5% resistance=330 package=THT]  # not connected
  LED1 = LED - 3mm [color="Red (633nm)" package="3 mm [THT]"]

nets:
  N1: Q1.base, U1.D2
  N2: Q1.collector, LED1.cathode
  N3: Q1.emitter, U1.GND, VCC1.-, U2.ADJ
  N4: U1.VCC, R1.Pin_0
  N5: VCC1.+, U2.IN
  N6: U2.OUT, R1.Pin_1
