# Fritzing sketch Blink LED (saved by Fritzing 0.9.3b)
breadboards: 1

parts:
  Part1 = Arduino Nano (Rev3.0)
  LED1 = LED - 5mm [color="Red (633nm)" package="5 mm [THT]"]

nets:
  N1: Part1.GND, LED1.cathode
  N2: Part1.D9, LED1.anode

notes:
  atMega328p, blink LED connected to D9 pin or PORTB1 (PB1)
